# Fritzing sketch ESInfaredControlledServo (saved by Fritzing 0.9.3b)
breadboards: 1

parts:
  Servo_Switch_(Motion_Toggles_HV_GND) = Basic Servo
  Arduino_Nano_(High_Voltage_Control) = Arduino Nano (Rev3.0)
  IR_Receiver = IR Receiver Breakout [package=PCB]
  LED1 = smd LED [color="Red (633nm)" package="0603 [SMD]"]
  LED2 = smd LED [color="Green (570nm)" package="0603 [SMD]"]
  R2 = Resistor [tolerance=±5% resistance=470 package="0805 [SMD]"]
  R3 = Resistor [tolerance=±5% resistance=470 package="0805 [SMD]"]
  Servo_Power_Supply_(DC_5V) = DC Power [voltage=5]
  HVPS_AC_Wall_Power_(120V) = AC Power [voltage=5 frequency=60]
  HVPS_SSR_(Connected_to_AC-DC_Power_Adapter) = RELAY-SOLIDSTATE [package=relay-s108t02]
  Servo_Power_Supply = 4 x AAA Battery Mount

nets:
  GND: Servo_Switch_(Motion_Toggles_HV_GND).gnd, Arduino_Nano_(High_Voltage_Control).GND, IR_Receiver.GND, R2.Pin_0, R3.Pin_0, Servo_Power_Supply_(DC_5V).V-, HVPS_AC_Wall_Power_(120V).V-, HVPS_SSR_(Connected_to_AC-DC_Power_Adapter).-, Servo_Power_Supply.-
  5V: Servo_Switch_(Motion_Toggles_HV_GND).vcc, Servo_Power_Supply_(DC_5V).V+, Servo_Power_Supply.+
  A5: Servo_Switch_(Motion_Toggles_HV_GND).pulse, Arduino_Nano_(High_Voltage_Control).A5
  N1: Arduino_Nano_(High_Voltage_Control).D2, LED2.anode
  N2: Arduino_Nano_(High_Voltage_Control).D3, LED1.anode
  N3: Arduino_Nano_(High_Voltage_Control).D11/MOSI, IR_Receiver.OUT
  5V_2: Arduino_Nano_(High_Voltage_Control).5V, IR_Receiver.VCC
  A0: Arduino_Nano_(High_Voltage_Control).A0, HVPS_SSR_(Connected_to_AC-DC_Power_Adapter).+
  N4: LED1.cathode, R2.Pin_1
  N5: LED2.cathode, R3.Pin_1
  N6: HVPS_AC_Wall_Power_(120V).V+, HVPS_SSR_(Connected_to_AC-DC_Power_Adapter).T2
  HVPS Adapter AC +: HVPS_SSR_(Connected_to_AC-DC_Power_Adapter).T1

notes:
  AC Ground (Wall)
  Note the SSR gets connected to the positive (+) of the AC-to-DC Adapter that is connected on the HVPS.
  Infared Controlled HV Servo Switch
