# Fritzing sketch ESPrinterSlaveInfaredSenderComponent (saved by Fritzing 0.9.3b)
breadboards: 1

parts:
  Arduino_Nano_(Infared_Sender) = Arduino Nano (Rev3.0)
  R4 = Resistor [tolerance=±5% resistance=470 package="0805 [SMD]"]
  IR1 = TSOP312.., 314.. [package=THT]

nets:
  GND (RAMPS 1.4/Mega): Arduino_Nano_(Infared_Sender).GND, IR1.GND
  N1: Arduino_Nano_(Infared_Sender).D3, IR1.Data
  N2: Arduino_Nano_(Infared_Sender).D12/MISO, R4.Pin_0
  5V: Arduino_Nano_(Infared_Sender).5V, IR1.Vs
  D44 (RAMPS 1.4/Mega): R4.Pin_1

notes:
  Note the ground of the Arduino must be connected to the ground of the 3D printer's Arduino Mega.
  3D Printer Infared Sender Slave
