# Fritzing sketch ESPrinterSlaveInfaredSender (saved by Fritzing 0.9.3b)
breadboards: 1

parts:
  Arduino_Nano_(Infared_Sender) = Arduino Nano (Rev3.0)
  D1 = LTE-302 [package=lte-302]
  R4 = Resistor [tolerance=±5% resistance=470 package="0805 [SMD]"]
  R3 = Resistor [tolerance=±5% resistance=330 package="0805 [SMD]"]

nets:
  GND (RAMPS 1.4/Mega): Arduino_Nano_(Infared_Sender).GND, R3.Pin_0
  N1: Arduino_Nano_(Infared_Sender).D3, D1.A
  N2: Arduino_Nano_(Infared_Sender).D12/MISO, R4.Pin_0
  N3: D1.C, R3.Pin_1
  D44 (RAMPS 1.4/Mega): R4.Pin_1

notes:
  Note the ground of the Arduino must be connected to the ground of the 3D printer's Arduino Mega.
  3D Printer Infared Sender Slave
